// Logisim project processor-surprise.circ as structural Verilog
module Datapath (
  output [4:0] TEST_25_21,
  output [31:0] R1,
  output [31:0] Y,
  output [31:0] v0,
  output [4:0] _20_16,
  output [4:0] _15_11,
  output [31:0] IMMEDIATE,
  output [31:0] INSTRUCTION
);

  wire alu_1_zero, branch_out, clock_1_out, controlunit_1_alusrc, controlunit_1_branch, controlunit_1_regdst,
       controlunit_1_regwrite;
  wire [2:0] bitselector_3_out, bitselector_4_out, bitselector_7_out, bitselector_8_out,
       controlunit_1_alucontrol, multiplexer_2_out;
  wire [4:0] bitselector_5_out;
  wire [7:0] adder_1_out, bit_extender_1_out, PC_q, shifter_1_out;
  wire [15:0] bitselector_9_out;
  wire [31:0] adder_2_out, bit_extender_2_out, multiplexer_1_out, multiplexer_3_out, registerfile_1_rd2,
       shifter_2_out, shifter_3_out;

  Multiplexer #(.width(32), .enable("false")) multiplexer_1 (
    .in0(bit_extender_2_out), .in1(adder_2_out), .out(multiplexer_1_out), .sel(branch_out));
  Clock clock_1 (.out(clock_1_out));
  Register PC (.D(bit_extender_1_out), .Q(PC_q), .clk(clock_1_out));  // open: en, clr
  Bit_Extender #(.in_width(32), .out_width(8)) bit_extender_1 (.in(multiplexer_1_out), .out(bit_extender_1_out));
  Shifter #(.shift("lr")) shifter_1 (.in(PC_q), .\dist (3'b010), .out(shifter_1_out));
  Adder adder_1 (.a(PC_q), .b(8'h4), .out(adder_1_out));  // open: cin, cout
  assign bit_extender_2_out = {{24{1'b0}}, adder_1_out};  // Bit_Extender bit_extender_2
  ROM #(.dataWidth(32)) rom_1 (.addr(shifter_1_out), .data(INSTRUCTION));  // open: sel
  Shifter #(.width(32), .shift("lr")) shifter_2 (.in(INSTRUCTION), .\dist (5'b01011), .out(shifter_2_out));
  ControlUnit controlunit_1 (
    .Instruction(INSTRUCTION), .RegDst(controlunit_1_regdst), .RegWrite(controlunit_1_regwrite),
    .ALUControl(controlunit_1_alucontrol), .Branch(controlunit_1_branch), .ALUSrc(controlunit_1_alusrc));
  BitSelector #(.width(32), .group(5)) bitselector_1 (.in(shifter_2_out), .out(TEST_25_21), .sel(3'b010));
  BitSelector #(.width(32), .group(5)) bitselector_2 (.in(shifter_2_out), .out(_20_16), .sel(3'b001));
  BitSelector #(.width(5), .group(3)) bitselector_3 (.in(TEST_25_21), .out(bitselector_3_out), .sel(1'b0));
  BitSelector #(.width(5), .group(3)) bitselector_4 (.in(_20_16), .out(bitselector_4_out), .sel(1'b0));
  BitSelector #(.width(32), .group(5)) bitselector_5 (.in(shifter_2_out), .out(bitselector_5_out), .sel(3'b001));
  BitSelector #(.width(32), .group(5)) bitselector_6 (.in(shifter_2_out), .out(_15_11), .sel(3'b000));
  RegisterFile registerfile_1 (
    .CLK(clock_1_out), .A1(bitselector_3_out), .WD3(Y), .A2(bitselector_4_out), .WE3(controlunit_1_regwrite),
    .RD1(R1), .RD2(registerfile_1_rd2), .A3(multiplexer_2_out), .V0(v0));
  BitSelector #(.width(5), .group(3)) bitselector_7 (.in(bitselector_5_out), .out(bitselector_7_out), .sel(1'b0));
  Multiplexer #(.width(3), .enable("false")) multiplexer_2 (
    .in0(bitselector_7_out), .in1(bitselector_8_out), .out(multiplexer_2_out), .sel(controlunit_1_regdst));
  BitSelector #(.width(5), .group(3)) bitselector_8 (.in(_15_11), .out(bitselector_8_out), .sel(1'b0));
  BitSelector #(.width(32), .group(16)) bitselector_9 (.in(INSTRUCTION), .out(bitselector_9_out), .sel(1'b0));
  Multiplexer #(.width(32), .enable("false")) multiplexer_3 (
    .in0(registerfile_1_rd2), .in1(IMMEDIATE), .out(multiplexer_3_out), .sel(controlunit_1_alusrc));
  assign IMMEDIATE = {{16{bitselector_9_out[15]}}, bitselector_9_out};  // Bit_Extender bit_extender_3
  ALU alu_1 (.B(multiplexer_3_out), .A(R1), .Y(Y), .in_1(controlunit_1_alucontrol), .Zero(alu_1_zero));
  Shifter #(.width(32)) shifter_3 (.in(IMMEDIATE), .\dist (5'b00010), .out(shifter_3_out));
  and branch (branch_out, controlunit_1_branch, alu_1_zero);
  Adder #(.width(32)) adder_2 (.a(shifter_3_out), .b(bit_extender_2_out), .out(adder_2_out));  // open: cin, cout

  // Notes on the sheet:
  //   Clock
  //   Next Instruction Setup
  //   ROM
  //   contents of rom_1 (hex, n*v repeats v):
  //   20040008 20050001 20020001 10a40003 20a50001 70451002 1000fffc 1000ffff
  //   Control Unit
  //   Register File
  //   Sign Extend
endmodule

module ALU (
  input  [2:0] in_1,
  input  [31:0] B,
  input  [31:0] A,
  output [31:0] Y,
  output Zero
);

  wire [31:0] adder_1_out, and_out, multiplexer_1_out, multiplexer_2_out, multiplier_1_out, not_1_out,
       or_out, shifter_1_out;

  Multiplexer #(.width(32), .enable("false")) multiplexer_1 (
    .in0(B), .in1(not_1_out), .out(multiplexer_1_out), .sel(in_1[2]));
  assign not_1_out = ~B;  // NOT_Gate not_1, 32 bits wide
  assign and_out = multiplexer_1_out & A;  // AND_Gate and, 32 bits wide
  assign or_out = multiplexer_1_out | A;  // OR_Gate or, 32 bits wide
  Adder #(.width(32)) adder_1 (.a(multiplexer_1_out), .b(A), .out(adder_1_out), .cin(in_1[2]));  // open: cout
  Multiplier #(.width(32)) multiplier_1 (.a(B), .b(A), .out(multiplier_1_out));  // open: cin, cout
  Shifter #(.width(32), .shift("lr")) shifter_1 (.in(adder_1_out), .\dist ({5{1'b1}}), .out(shifter_1_out));
  Multiplexer #(.width(32), .enable("false")) multiplexer_2 (
    .in0(multiplier_1_out), .in1(shifter_1_out), .out(multiplexer_2_out), .sel(in_1[2]));
  Multiplexer #(.select(2), .width(32), .enable("false")) multiplexer_3 (
    .in0(and_out), .in1(or_out), .in2(adder_1_out), .in3(multiplexer_2_out), .out(Y), .sel(in_1[1:0]));
  Comparator #(.width(32), .mode("unsigned")) comparator_1 (.a(Y), .b({32{1'b0}}), .eq(Zero));  // open: gt, lt
endmodule

module Tests (
  output [31:0] Y,
  output [7:0] out_2,
  output [7:0] out_3,
  output [2:0] out_4
);

  BitSelector #(.width(32), .group(8)) bitselector_1 (.in(32'h12356789), .out(out_2), .sel(2'b01));
  BitSelector #(.width(32), .group(8)) bitselector_2 (.in(32'h12356789), .out(out_3), .sel(2'b01));
  BitSelector #(.group(3)) bitselector_3 (.in(out_3), .out(out_4), .sel(2'b00));

  assign Y = 32'hf4010207;

  // Notes on the sheet:
  //   binary values in Logisim. Convince yourself how the bits are displayed.
  //   Example 2: The bit selector is configured to have 32  
  //   bit group #1 (starting at index 0) is selected for the output.
  //   That is, the 8 bits 0x67 at bit indices 15..8  are sent to the output.
  //   Example 3: Now, assume that you want to extract 3 bits at   
  //   Example 1: A simple example that illustrates how 32-bit values are displayed as 
  //   input bits and 8 output bits. The parameter constant is 1, which means that   
  //   bit indices 10..8. This can be accoplished by putting two bit selecotrs in series.
endmodule

module RegisterFile (
  input  CLK,
  input  [2:0] A1,
  input  [31:0] WD3,
  input  [2:0] A2,
  input  WE3,
  input  [2:0] A3,
  output [31:0] RD1,
  output [31:0] RD2,
  output [31:0] V0
);

  wire and_1_out, and_2_out, and_3_out, and_4_out, and_5_out, and_6_out, and_7_out, decoder_1_out0,
       decoder_1_out1, decoder_1_out2, decoder_1_out3, decoder_1_out4, decoder_1_out5, decoder_1_out6,
       decoder_1_out7;
  wire [31:0] _0_q, a0_q, a1_q, a2_q, a3_q, at_q, v1_q;

  Decoder #(.select(3)) decoder_1 (
    .out0(decoder_1_out0), .out1(decoder_1_out1), .out2(decoder_1_out2), .out3(decoder_1_out3),
    .out4(decoder_1_out4), .out5(decoder_1_out5), .out6(decoder_1_out6), .out7(decoder_1_out7), .sel(A3));  // open: en
  and and_1 (and_1_out, WE3, decoder_1_out1);
  and and_2 (and_2_out, WE3, decoder_1_out2);
  and and_3 (and_3_out, WE3, decoder_1_out3);
  and and_4 (and_4_out, WE3, decoder_1_out4);
  and and_5 (and_5_out, WE3, decoder_1_out5);
  and and_6 (and_6_out, WE3, decoder_1_out6);
  and and_7 (and_7_out, WE3, decoder_1_out7);
  Register #(.width(32)) _0 (.D({32{1'b0}}), .en(decoder_1_out0), .Q(_0_q), .clk(CLK));  // open: clr
  Register #(.width(32)) at (.D(WD3), .en(and_1_out), .Q(at_q), .clk(CLK));  // open: clr
  Register #(.width(32)) u_v0 (.D(WD3), .en(and_2_out), .Q(V0), .clk(CLK));  // open: clr
  Register #(.width(32)) v1 (.D(WD3), .en(and_3_out), .Q(v1_q), .clk(CLK));  // open: clr
  Register #(.width(32)) a0 (.D(WD3), .en(and_4_out), .Q(a0_q), .clk(CLK));  // open: clr
  Register #(.width(32)) u_a1 (.D(WD3), .en(and_5_out), .Q(a1_q), .clk(CLK));  // open: clr
  Register #(.width(32)) u_a2 (.D(WD3), .en(and_6_out), .Q(a2_q), .clk(CLK));  // open: clr
  Register #(.width(32)) u_a3 (.D(WD3), .en(and_7_out), .Q(a3_q), .clk(CLK));  // open: clr
  Multiplexer #(.select(3), .width(32)) multiplexer_1 (
    .in0(_0_q), .in1(at_q), .in2(V0), .in3(v1_q), .in4(a0_q), .in5(a1_q), .in6(a2_q), .in7(a3_q), .out(RD1),
    .sel(A1));  // open: en
  Multiplexer #(.select(3), .width(32)) multiplexer_2 (
    .in0(_0_q), .in1(at_q), .in2(V0), .in3(v1_q), .in4(a0_q), .in5(a1_q), .in6(a2_q), .in7(a3_q), .out(RD2),
    .sel(A2));  // open: en
endmodule

module ControlUnit (
  input  [31:0] Instruction,
  output RegDst,
  output RegWrite,
  output ALUSrc,
  output [2:0] ALUControl,
  output Branch
);

  wire comparator_2_eq, comparator_4_eq;
  wire [2:0] bit_extender_1_out, bit_extender_2_out, or_3_out, shifter_2_out;
  wire [5:0] bitselector_1_out;
  wire [31:0] shifter_1_out;

  Shifter #(.width(32), .shift("lr")) shifter_1 (.in(Instruction), .\dist (5'b11010), .out(shifter_1_out));
  BitSelector #(.width(32), .group(6)) bitselector_1 (.in(shifter_1_out), .out(bitselector_1_out), .sel(3'b000));
  Comparator #(.width(6), .mode("unsigned")) comparator_1 (
    .a(bitselector_1_out), .b(6'b001000), .eq(ALUSrc));  // open: gt, lt
  Comparator #(.width(6), .mode("unsigned")) comparator_2 (
    .a(bitselector_1_out), .b({6{1'b0}}), .eq(comparator_2_eq));  // open: gt, lt
  Comparator #(.width(6), .mode("unsigned")) comparator_3 (
    .a(bitselector_1_out), .b(6'b000100), .eq(Branch));  // open: gt, lt
  Comparator #(.width(6), .mode("unsigned")) comparator_4 (
    .a(bitselector_1_out), .b(6'b011100), .eq(comparator_4_eq));  // open: gt, lt
  assign bit_extender_1_out = {{2{1'b0}}, Branch};  // Bit_Extender bit_extender_1
  assign bit_extender_2_out = {{2{1'b0}}, comparator_4_eq};  // Bit_Extender bit_extender_2
  or or_1 (RegDst, comparator_2_eq, comparator_4_eq);
  Shifter #(.width(3)) shifter_2 (.in(bit_extender_1_out), .\dist (2'b10), .out(shifter_2_out));
  or or_2 (RegWrite, ALUSrc, comparator_4_eq, RegDst);
  assign or_3_out = shifter_2_out | bit_extender_2_out;  // OR_Gate or_3, 3 bits wide
  Adder #(.width(3)) adder_1 (.a(or_3_out), .b(3'b010), .out(ALUControl));  // open: cin, cout
endmodule
